# Fritzing sketch WS_Probe (saved by Fritzing 0.9.3b)
breadboards: 1

parts:
  Part1 = Arduino Uno (Rev3)
  DHT22 = Humidity and Temperature Sensor RHT03
  R1 = Resistor [tolerance=±5% resistance=10k package=THT]
  Part2 = Real Time Clock Module - DS1307 RTC Breakout Board
  U3 = TEMPERATURE-SENSOR [package=to-92]
  R2 = Resistor [tolerance=±5% resistance=4.7k package=THT]
  TFT1 = 1.8" TFT Display with uSD
  Part4 = MPL3115A2 I2C Barometric Pressure, Altitude, Temperature Sensor

nets:
  N1: Part1.D8, TFT1.RST
  N2: Part1.D9_PWM, TFT1.D/C
  N3: Part1.D10_PWM/SS, TFT1.CS
  N4: Part1.D11_PWM/MOSI, TFT1.MOSI
  N5: Part1.D13/SCK, TFT1.SCK
  N6: Part1.A4/SDA, Part2.SDA, Part4.SCL
  N7: Part1.A5/SCL, Part2.SCL, Part4.SDA
  N8: Part1.D2, DHT22.Data-signal, R1.Pin_1
  N9: Part1.D5_PWM, U3.GND, R2.Pin_1
  N10: Part1.D7, Part1.RESET
  VCC: Part1.5V, DHT22.Vcc, R1.Pin_0, Part2.5V, U3.VCC, R2.Pin_0, TFT1.VCC, Part4.VIN
  GND: Part1.GND, DHT22.GND_2, Part2.GND, U3.ADJ, TFT1.GND, Part4.GND

notes:
  10K Ohm pullup
  SainSmart 1.8" TFT, not Adafruit
  Ignore TFT pin positions -- couldn't edit
  Use Uno pin numbers, check TFT labels
  SCL - 13 (Adafruit SCK)
  SDA - 11 (Adafruit MOSI)
  RS/DC - 9 (Adafruit D/C)
  Reset - 8 (Adafruit Reset)
  CS - 10 (Adafruit CS)
  TFT uses its own Uno pins for SDA/SCL (11+13) rather than the SDA/SCL buss
  DHT22
  temp/humidity
  pin 3 no conn.
  4.7K Ohm pullup
  DS18B20 Temp Sensors in parallel, 1m cable (multiple)
  Adafruit MPL3115A2
  alt/baro/temp @ 5v
  Chronodot
  SDA
  SCL
  DHT22 Data
  DS18B20 Data
  WeatherProbe
  Arduino Circuit
  hdtodd@gmail.com
  2018\01\14
  Enable Arduino hardware reset from program code (if missing, TFT doesn't reset on restart command)

custom parts:
  1.8" TFT Display with uSD: 1.8" TFT Display with SPI control and MicroSD card
  MPL3115A2 I2C Barometric Pressure, Altitude, Temperature Sensor: This pressure sensor from Freescale is a great low-cost sensing solution for precision measurement of barometric pressure and altitude. The MPL3115A2 has a typical 1.5 Pascal resolution, which can resolve altitude at 0.3 meters (compare to the BMP180 which can do 0.17m). It has some upsides compared to the BMP180, such as interrupt outputs for ultra-low power usage, and its also a heck of a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
